// Logisim project A4.circ as structural Verilog: 2 circuits, main circuit main
module main (
  input  in_1,
  input  in_2,
  input  in_3,
  input  in_4,
  input  [31:0] in_5,
  input  in_6,
  input  in_7,
  input  in_8,
  input  in_9,
  output [31:0] out_10,
  output [31:0] out_11
);

  wire clk;
  wire [2:0] selectRA, selectRB, selectRY;
  wire [31:0] Register_File_ra, Register_File_rb;

  RegisterFile Register_File (
    .RA(Register_File_ra), .Address_RA(selectRA), .Address_RY(selectRY), .RB(Register_File_rb),
    .Address_RB(selectRB), .RY(in_5), .clk(clk), .enRA(in_2), .enRB(in_3), .enRY(in_4), .clr(in_1));
  Register #(.width(32)) RA (.D(Register_File_ra), .en(in_6), .Q(out_10), .clk(clk), .clr(in_8));
  Register #(.width(32)) RB (.D(Register_File_rb), .en(in_7), .Q(out_11), .clk(clk), .clr(in_9));
  Clock clock_1 (.out(clk));

  // Other names for the same wires on the sheet: clr = in_1; clrRA = in_8; clrRB = in_9; enRA = in_6; enRB = in_7;
  //   enSelectRA = in_2; enSelectRB = in_3; enSelectRY = in_4; OutRA[31:0] = out_10; OutRB[31:0] = out_11;
  //   RY[31:0] = in_5
endmodule

module RegisterFile (
  input  enRA,
  input  [2:0] Address_RA,
  input  enRY,
  input  [2:0] Address_RY,
  input  enRB,
  input  [2:0] Address_RB,
  input  clk,
  input  clr,
  input  [31:0] RY,
  output [31:0] RA,
  output [31:0] RB
);

  wire demultiplexer_1_out0, demultiplexer_1_out1, demultiplexer_1_out2, demultiplexer_1_out3,
       demultiplexer_1_out4, demultiplexer_1_out5, demultiplexer_1_out6, demultiplexer_1_out7;
  wire [31:0] R1_q, R2_q, R3_q, R4_q, R5_q, R6_2_q, R6_q, R7_q;

  Demultiplexer #(.select(3)) demultiplexer_1 (
    .out0(demultiplexer_1_out0), .out1(demultiplexer_1_out1), .out2(demultiplexer_1_out2),
    .out3(demultiplexer_1_out3), .out4(demultiplexer_1_out4), .out5(demultiplexer_1_out5),
    .out6(demultiplexer_1_out6), .out7(demultiplexer_1_out7), .in(1'b1), .sel(Address_RY), .en(enRY));
  Register #(.width(32)) R1 (.D(RY), .en(demultiplexer_1_out0), .Q(R1_q), .clk(clk), .clr(clr));
  Register #(.width(32)) R2 (.D(RY), .en(demultiplexer_1_out1), .Q(R2_q), .clk(clk), .clr(clr));
  Register #(.width(32)) R3 (.D(RY), .en(demultiplexer_1_out2), .Q(R3_q), .clk(clk), .clr(clr));
  Register #(.width(32)) R4 (.D(RY), .en(demultiplexer_1_out3), .Q(R4_q), .clk(clk), .clr(clr));
  Register #(.width(32)) R5 (.D(RY), .en(demultiplexer_1_out4), .Q(R5_q), .clk(clk), .clr(clr));
  Register #(.width(32)) R6 (.D(RY), .en(demultiplexer_1_out5), .Q(R6_q), .clk(clk), .clr(clr));
  Register #(.width(32)) R6_2 (.D(RY), .en(demultiplexer_1_out6), .Q(R6_2_q), .clk(clk), .clr(clr));
  Register #(.width(32)) R7 (.D(RY), .en(demultiplexer_1_out7), .Q(R7_q), .clk(clk), .clr(clr));
  Multiplexer #(.select(3), .width(32)) multiplexer_1 (
    .in0(R1_q), .in1(R2_q), .in2(R3_q), .in3(R4_q), .in4(R5_q), .in5(R6_q), .in6(R6_2_q), .in7(R7_q),
    .out(RA), .sel(Address_RA), .en(enRA));
  Multiplexer #(.select(3), .width(32)) multiplexer_2 (
    .in0(R1_q), .in1(R2_q), .in2(R3_q), .in3(R4_q), .in4(R5_q), .in5(R6_q), .in6(R6_2_q), .in7(R7_q),
    .out(RB), .sel(Address_RB), .en(enRB));

  // Notes on the sheet:
  //   19CS01065
  //   Register File
endmodule
